// Logisim project KrajcovicPPI02.circ as structural Verilog: 1 circuit, main circuit main
module main (
  input  a,
  input  b,
  input  c,
  input  d,
  output A_D,
  output B_D,
  output C_D,
  output D_D,
  output E_D,
  output A_K,
  output B_K,
  output C_K,
  output D_K,
  output E_K
);

  wire a_____c_____d_out, a____c____d_out, a____c__d_out, a___b_2_out, a___b_out, a___c_2_out, a___c_d_out,
       a___c_out, a__c____d_out, a__c___d_out, a__c__d_out, a_c__d_out, b__c_2_out, b__c_out, b_c_2_out,
       b_c_out, b_d_2_out, b_d_out, c___d_2_out, c___d_out, na_2_out, na_out, nc_2_out, nc_out, nd_2_out,
       nd_3_out;

  nand na (na_out, a, a);
  nor na_2 (na_2_out, a, a);
  // NAND_Gate nd has open pins: in0=b, in1=b, out=open
  nand nc (nc_out, c, c);
  nor nc_2 (nc_2_out, c, c);
  // NOR_Gate nb has open pins: in0=b, in1=b, out=open
  nand nd_2 (nd_2_out, d, d);
  nor nd_3 (nd_3_out, d, d);
  nand a___b (a___b_out, na_out, b);
  nand a___c (a___c_out, na_out, c);
  nand b_c (b_c_out, b, c);
  nand b__c (b__c_out, b, nc_out);
  nand u_b_d (b_d_out, b, d);
  nand c___d (c___d_out, nc_out, d);
  nand a_____c_____d (a_____c_____d_out, na_out, nc_out, nd_2_out);
  nand a____c__d (a____c__d_out, na_out, c, d);
  nand a__c____d (a__c____d_out, a, nc_out, d);
  nand a__c__d (a__c__d_out, a, c, nd_2_out);
  nor b_c_2 (b_c_2_out, b, c);
  nor a___c_2 (a___c_2_out, na_2_out, c);
  nor a___b_2 (a___b_2_out, na_2_out, b);
  nor b__c_2 (b__c_2_out, b, nc_2_out);
  nor b_d_2 (b_d_2_out, b, d);
  nor c___d_2 (c___d_2_out, nc_2_out, d);
  nor a___c_d (a___c_d_out, na_2_out, c, d);
  nor a_c__d (a_c__d_out, a, c, nd_3_out);
  nor a__c___d (a__c___d_out, a, nc_2_out, d);
  nor a____c____d (a____c____d_out, na_2_out, nc_2_out, nd_3_out);
  nand a___b____a___c___b_c (B_D, a___b_out, a___c_out, b_c_out);
  nand b__c_____b_d____c___d (C_D, b__c_out, b_d_out, c___d_out);
  nand a_____c____d____a____c__d___a__c____d___a__c__d (D_D, a_____c_____d_out, a____c__d_out, a__c____d_out, a__c__d_out);
  nor b___c____a___c____a___b (B_K, b_c_2_out, a___c_2_out, a___b_2_out);
  nor b__c_____b_d____c___d_2 (C_K, b__c_2_out, b_d_2_out, c___d_2_out);
  nor a___c_d___a_c__d_____a__c___d____a____c____d (D_K, a___c_d_out, a_c__d_out, a__c___d_out, a____c____d_out);

  assign A_D = a;
  assign A_K = a;
  assign E_D = d;
  assign E_K = d;
endmodule
